# Fritzing sketch temperature_node (saved by Fritzing 0.9.2b)

parts:
  Part1 = Arduino Pro Mini v13
  NRF24L1 = NRF24L01
  Part2 = Digital Temperature Sensor Breakout - TMP102
  U1 = L6920D [package=tsop8]
  VCC1 = Battery

nets:
  N1: Part1.A4, Part2.SDA
  N2: Part1.A5, Part2.SCL
  N3: Part1.RAW, U1.VOUT
  GND: Part1.GND, NRF24L1.GND, Part2.GND
  VCC: Part1.VCC, NRF24L1.VCC, Part2.V+
  N4: Part1.A2, U1.VIN, VCC1.+
  N5: Part1.D13/SCK, NRF24L1.SCK
  N6: Part1.D12/MISO, NRF24L1.MISO
  N7: Part1.D11_PWM/MOSI, NRF24L1.MOSI
  N8: Part1.D7, NRF24L1.CE
  N9: Part1.D6_PWM, NRF24L1.CSN
  N10: U1.GND, VCC1.-

custom parts:
  NRF24L01: NRF24L01 module
  L6920D: DC to DC Booster
